# Fritzing sketch chair (saved by Fritzing 0.9.3b)
breadboards: 1

parts:
  Part1 = Arduino Nano (Rev3.0)
  BAT1 = BC9VPC [package=bc9vpc]
  J1 = Basic Force Sensing Resistor (FSR) [package=THT]
  R1 = Resistor [tolerance=±5% resistance=22k package="0805 [SMD]"]

nets:
  N1: Part1.GND, BAT1.V-, J1.pin_0
  N2: Part1.VIN, BAT1.V+
  N3: Part1.A7, J1.pin_1, R1.Pin_0
  N4: Part1.3V3, R1.Pin_1
