# Fritzing sketch control (saved by Fritzing 0.9.3b)
breadboards: 1

parts:
  Part1 = Arduino Nano (Rev3.0)
  R1 = Resistor [tolerance=±5% resistance=460 package=THT]
  J1 = Dagu DGServo 9g header (male) [package=THT]
  J2 = Power Jack [package=power_jack_slot]
  JP1 = Header 10 [package=1x10-2mm-smd]
  J4 = Basic Servo
  Part2 = LilyPad Tri-Color LED
  J3 = Basic Servo

nets:
  GND: Part1.GND, J1.gnd, J2.GND, JP1.7, JP1.10, J4.gnd, J3.gnd
  N1: Part1.D3, JP1.5, J3.pulse
  N2: Part1.D5, JP1.8, J4.pulse
  N3: Part1.D6, R1.Pin_0
  N4: Part1.D10, JP1.3, Part2.B
  N5: Part1.D11/MOSI, JP1.2, Part2.G
  N6: Part1.D12/MISO, JP1.1, Part2.R
  VCC: Part1.3V3, JP1.4, JP1.6, JP1.9, J4.vcc, Part2.+, J3.vcc
  N7: R1.Pin_1, J1.DIN
  N8: J1.Vcc, J2.PWR

custom parts:
  Dagu DGServo 9g header (male): Dagu DGServo 9g header (male) This part is a minor variation of the standard three pin header; in schematic view the pins have been labelled to show clearly pulse, Vcc and ground. Plug this header into a breadboard, stripboard or PCB to allow a servo header female connector plug (e.g. on the Dagu DGServo 9g) to be connected to the board.
