# Fritzing sketch door (saved by Fritzing 0.9.3b)
breadboards: 1

parts:
  Part1 = Arduino Nano (Rev3.0)
  BAT1 = BC9VPC [package=bc9vpc]
  R1 = Resistor [tolerance=±5% resistance=220 package="0805 [SMD]"]
  S1 = Reed switch [package=THT]

nets:
  N1: Part1.GND, BAT1.V-, S1.pin_2
  N2: Part1.VIN, BAT1.V+
  N3: Part1.A7, R1.Pin_0, S1.pin_1
  N4: Part1.3V3, R1.Pin_1
