# Fritzing sketch table (saved by Fritzing 0.9.3b)
breadboards: 1

parts:
  Part1 = Arduino Nano (Rev3.0)
  BAT1 = BC9VPC [package=bc9vpc]
  R1 = Resistor [tolerance=±5% resistance=22k package=THT]
  R2 = Resistor [tolerance=±5% resistance=22k package=THT]
  Q1 = LTR-301 [package=ltr-301]
  Q2 = LTR-301 [package=ltr-301]

nets:
  N1: Part1.GND, BAT1.V-, Q1.E, Q2.E
  N2: Part1.VIN, BAT1.V+
  N3: Part1.A7, R2.Pin_0, Q2.C
  N4: Part1.A6, R1.Pin_0, Q1.C
  N5: Part1.3V3, R1.Pin_1, R2.Pin_1
